# Fritzing sketch breadboard (saved by Fritzing 0.9.3b)
breadboards: 4

parts:
  MCU = IC, DIP package, 40 pins [chip_label="Atmega 162"]
  RESET = Pushbutton [package="[SMD]"]
  LED = LED - 3mm [color="Red (633nm)" package="3 mm [THT]"]

nets:
  N1: MCU.pin1, LED.anode
  N2: MCU.pin9, RESET.Pin_1, RESET.Pin_2
  N3: RESET.Pin_3, RESET.Pin_4, LED.cathode
